// Logisim project logisim_sim1.circ as structural Verilog: 7 circuits, main circuit main
module main (
  input  Clock,
  input  Selector,
  input  [15:0] \input ,
  output [15:0] \output 
);

  wire and_1_out, clock_1_out, cpu_1_halt, cpu_1_ram_clock, cpu_1_ram_store, multiplexer_1_out, not_1_out,
       Reset_out;
  wire [15:0] cpu_1_ram_data_out, ram_1_data;
  wire [23:0] cpu_1_ram_address;

  Button Reset (.out(Reset_out));
  Clock clock_1 (.out(clock_1_out));
  not not_1 (not_1_out, cpu_1_halt);
  Button button_1 ();  // open: out
  Multiplexer #(.enable("false")) multiplexer_1 (
    .in0(Clock), .in1(clock_1_out), .out(multiplexer_1_out), .sel(and_1_out));
  and and_1 (and_1_out, Selector, not_1_out);
  CPU cpu_1 (
    .Reset(Reset_out), .Clock(multiplexer_1_out), .\input (\input ), .RAM_DATA_In(ram_1_data),
    .\output (\output ), .halt(cpu_1_halt), .Ram_Address(cpu_1_ram_address),
    .RAM_DATA_Out(cpu_1_ram_data_out), .RAM_Clock(cpu_1_ram_clock), .Ram_store(cpu_1_ram_store));
  RAM #(.addrWidth(24), .dataWidth(16), .bus("separate")) ram_1 (
    .addr(cpu_1_ram_address), .din(cpu_1_ram_data_out), .data(ram_1_data), .str(cpu_1_ram_store),
    .clk(cpu_1_ram_clock));  // open: sel, ld, clr

  // Notes on the sheet:
  //   RAM
endmodule

module instruction_word_decoder (
  input  [3:0] Instruction,
  output Math,
  output Comp,
  output Shift,
  output load_into_reg,
  output addi,
  output send_into_ram,
  output jump_to_address,
  output jump_number,
  output halt
);

  wire decoder_1_out0, decoder_1_out1, decoder_1_out2, decoder_1_out3, decoder_1_out4, decoder_1_out5,
       decoder_1_out6, decoder_1_out7, decoder_1_out8;

  Decoder #(.select(4), .enable("false")) decoder_1 (
    .out0(decoder_1_out0), .out1(decoder_1_out1), .out2(decoder_1_out2), .out3(decoder_1_out3),
    .out4(decoder_1_out4), .out5(decoder_1_out5), .out6(decoder_1_out6), .out7(decoder_1_out7),
    .out8(decoder_1_out8), .out9(Shift), .out10(addi), .out11(load_into_reg), .out12(send_into_ram),
    .out13(jump_to_address), .out14(jump_number), .out15(halt), .sel(Instruction));
  or u_math (Math, decoder_1_out0, decoder_1_out1, decoder_1_out2, decoder_1_out3);
  or u_comp (Comp, decoder_1_out4, decoder_1_out5, decoder_1_out6, decoder_1_out7, decoder_1_out8);

  // Notes on the sheet:
  //   load into reg
  //   send to ram
endmodule

module ALU (
  input  [3:0] instruction,
  input  [15:0] input1,
  input  [15:0] input2,
  input  [3:0] input_2_const,
  output [15:0] destination_output
);

  wire comparator_1_lt, comparator_2_eq, comparator_2_gt, comparator_2_lt, instruction_word_decoder_1_addi,
       instruction_word_decoder_1_comp, instruction_word_decoder_1_math, instruction_word_decoder_1_shift,
       or_1_out;
  wire [1:0] priority_encoder_1_out;
  wire [3:0] negator_1_out;
  wire [15:0] adder_1_out, adder_2_out, and_1_out, divider_1_out, multiplexer_1_out, multiplexer_3_out,
       multiplier_1_out, nor_1_out, or_2_out, shifter_1_out, shifter_2_out, subtractor_1_out, xor_1_out;

  instruction_word_decoder instruction_word_decoder_1 (
    .Instruction(instruction), .Math(instruction_word_decoder_1_math),
    .Comp(instruction_word_decoder_1_comp), .Shift(instruction_word_decoder_1_shift),
    .addi(instruction_word_decoder_1_addi));  // open: load_into_reg, send_into_ram, jump_to_address, jump_number, halt
  or or_1 (or_1_out, instruction_word_decoder_1_math, instruction_word_decoder_1_comp, instruction_word_decoder_1_shift, instruction_word_decoder_1_addi);
  Negator #(.width(4)) negator_1 (.in(input_2_const), .out(negator_1_out));
  Comparator #(.width(4)) comparator_1 (.a(input_2_const), .b(4'b0000), .lt(comparator_1_lt));  // open: gt, eq
  Adder #(.width(16)) adder_1 (.a(input1), .b(input2), .out(adder_1_out));  // open: cin, cout
  Subtractor #(.width(16)) subtractor_1 (.a(input1), .b(input2), .out(subtractor_1_out));  // open: bin, bout
  Multiplier #(.width(16)) multiplier_1 (.a(input1), .b(input2), .out(multiplier_1_out));  // open: cin, cout
  Divider #(.width(16)) divider_1 (.a(input1), .b(input2), .out(divider_1_out));  // open: upper, rem
  assign and_1_out = input1 & input2;  // AND_Gate and_1, 16 bits wide
  assign or_2_out = input1 | input2;  // OR_Gate or_2, 16 bits wide
  assign nor_1_out = ~(input1 | input2);  // NOR_Gate nor_1, 16 bits wide
  assign xor_1_out = input1 ^ input2;  // XOR_Gate xor_1, 16 bits wide
  Comparator #(.width(16)) comparator_2 (
    .a(input1), .b(input2), .gt(comparator_2_gt), .eq(comparator_2_eq), .lt(comparator_2_lt));
  Adder #(.width(16)) adder_2 (.a(input1), .b({{12{1'b0}}, input_2_const}), .out(adder_2_out));  // open: cin, cout
  Priority_Encoder #(.select(2), .disabled(0)) priority_encoder_1 (
    .in0(comparator_2_gt), .in1(comparator_2_eq), .in2(comparator_2_lt), .out(priority_encoder_1_out));  // open: in3, gs, en_out, en_in
  Shifter #(.width(16), .shift("lr")) shifter_1 (.in(input1), .\dist (input_2_const), .out(shifter_1_out));
  Shifter #(.width(16)) shifter_2 (.in(input1), .\dist (negator_1_out), .out(shifter_2_out));
  Multiplexer #(.width(16), .enable("false")) multiplexer_1 (
    .in0(shifter_1_out), .in1(shifter_2_out), .out(multiplexer_1_out), .sel(comparator_1_lt));
  Multiplexer #(.select(4), .width(16)) multiplexer_2 (
    .in0(adder_1_out), .in1(subtractor_1_out), .in2(multiplier_1_out), .in3(divider_1_out), .in4(and_1_out),
    .in5(or_2_out), .in6(nor_1_out), .in7(xor_1_out), .in8(multiplexer_3_out), .in9(multiplexer_1_out),
    .in10(adder_2_out), .out(destination_output), .sel(instruction), .en(or_1_out));  // open: in11, in12, in13, in14, in15
  Multiplexer #(.select(2), .width(16), .disabled(0), .enable("false")) multiplexer_3 (
    .in0(16'h1), .in1({16{1'b0}}), .in2({16{1'b1}}), .out(multiplexer_3_out), .sel(priority_encoder_1_out));  // open: in3

  // Notes on the sheet:
  //   addi
endmodule

module Registers (
  input  Clock,
  input  Reset,
  input  [3:0] Instruction,
  input  [15:0] ALU_Input_data,
  input  [3:0] ALU_Output_1_Address,
  input  [3:0] RAM_Output_Address,
  input  [15:0] RAM_Input_data,
  input  [3:0] Jump_reg_check_Output_Address,
  input  [3:0] ALU_Output_2_Address,
  input  [3:0] ALU_Input_data_address,
  input  [3:0] RAM_input_data_address,
  input  counter_clock,
  input  [15:0] user_input,
  input  ram_counter_overflow,
  output [15:0] output_Data_Jump,
  output [15:0] output_Data_Ram,
  output [15:0] output_1_Data_ALU,
  output [15:0] ALU_Output_2_Data,
  output [15:0] ram_data_address_extension,
  output [15:0] instruction_address_extension,
  output [15:0] user_output
);

  wire decoder_1_out1, decoder_1_out2, decoder_1_out3, decoder_1_out4, decoder_1_out5, decoder_1_out6,
       decoder_1_out7, decoder_1_out8, decoder_1_out9, decoder_1_out10, decoder_1_out11, decoder_1_out12,
       decoder_1_out13, decoder_1_out14, decoder_1_out15, instruction_word_decoder_1_addi,
       instruction_word_decoder_1_comp, instruction_word_decoder_1_jump_number,
       instruction_word_decoder_1_jump_to_address, instruction_word_decoder_1_load_into_reg,
       instruction_word_decoder_1_math, instruction_word_decoder_1_send_into_ram,
       instruction_word_decoder_1_shift, or_1_out, or_2_out, or_3_out, or_4_out, or_5_out, or_6_out, or_7_out;
  wire [3:0] multiplexer_2_out, multiplexer_6_out, multiplexer_7_out;
  wire [15:0] adder_1_out, multiplexer_1_out, multiplexer_3_out, register_1_q, register_2_q, register_3_q,
       register_4_q, register_5_q, register_6_q, register_7_q, register_8_q, register_9_q, register_10_q,
       register_11_q, register_12_q;

  instruction_word_decoder instruction_word_decoder_1 (
    .Instruction(Instruction), .Math(instruction_word_decoder_1_math),
    .Comp(instruction_word_decoder_1_comp), .load_into_reg(instruction_word_decoder_1_load_into_reg),
    .Shift(instruction_word_decoder_1_shift), .send_into_ram(instruction_word_decoder_1_send_into_ram),
    .jump_to_address(instruction_word_decoder_1_jump_to_address),
    .jump_number(instruction_word_decoder_1_jump_number), .addi(instruction_word_decoder_1_addi));  // open: halt
  or or_1 (or_1_out, instruction_word_decoder_1_math, instruction_word_decoder_1_comp, instruction_word_decoder_1_shift, instruction_word_decoder_1_addi);
  or or_2 (or_2_out, instruction_word_decoder_1_jump_to_address, instruction_word_decoder_1_jump_number);
  Multiplexer #(.width(16)) multiplexer_1 (
    .in0(ALU_Input_data), .in1(RAM_Input_data), .out(multiplexer_1_out),
    .sel(instruction_word_decoder_1_load_into_reg), .en(or_3_out));
  or or_3 (or_3_out, or_1_out, instruction_word_decoder_1_load_into_reg);
  Decoder #(.select(4), .disabled(0)) decoder_1 (
    .out1(decoder_1_out1), .out2(decoder_1_out2), .out3(decoder_1_out3), .out4(decoder_1_out4),
    .out5(decoder_1_out5), .out6(decoder_1_out6), .out7(decoder_1_out7), .out8(decoder_1_out8),
    .out9(decoder_1_out9), .out10(decoder_1_out10), .out11(decoder_1_out11), .out12(decoder_1_out12),
    .out13(decoder_1_out13), .out14(decoder_1_out14), .out15(decoder_1_out15), .sel(multiplexer_2_out),
    .en(or_3_out));  // open: out0
  Multiplexer #(.width(4), .enable("false")) multiplexer_2 (
    .in0(ALU_Input_data_address), .in1(RAM_input_data_address), .out(multiplexer_2_out),
    .sel(instruction_word_decoder_1_load_into_reg));
  or or_4 (or_4_out, decoder_1_out14, ram_counter_overflow);
  Multiplexer #(.width(16), .enable("false")) multiplexer_3 (
    .in0(multiplexer_1_out), .in1(adder_1_out), .out(multiplexer_3_out), .sel(ram_counter_overflow));
  or or_5 (or_5_out, counter_clock, Clock);
  Adder #(.width(16)) adder_1 (.a(instruction_address_extension), .b(16'h1), .out(adder_1_out));  // open: cin, cout
  Register #(.width(16)) register_1 (
    .D(multiplexer_1_out), .en(decoder_1_out1), .Q(register_1_q), .clk(Clock), .clr(Reset));
  Register #(.width(16)) register_2 (
    .D(multiplexer_1_out), .en(decoder_1_out2), .Q(register_2_q), .clk(Clock), .clr(Reset));
  Register #(.width(16)) register_3 (
    .D(multiplexer_1_out), .en(decoder_1_out3), .Q(register_3_q), .clk(Clock), .clr(Reset));
  Register #(.width(16)) register_4 (
    .D(multiplexer_1_out), .en(decoder_1_out4), .Q(register_4_q), .clk(Clock), .clr(Reset));
  Register #(.width(16)) register_5 (
    .D(multiplexer_1_out), .en(decoder_1_out5), .Q(register_5_q), .clk(Clock), .clr(Reset));
  Register #(.width(16)) register_6 (
    .D(multiplexer_1_out), .en(decoder_1_out6), .Q(register_6_q), .clk(Clock), .clr(Reset));
  Register #(.width(16)) register_7 (
    .D(multiplexer_1_out), .en(decoder_1_out7), .Q(register_7_q), .clk(Clock), .clr(Reset));
  Register #(.width(16)) register_8 (
    .D(multiplexer_1_out), .en(decoder_1_out8), .Q(register_8_q), .clk(Clock), .clr(Reset));
  Register #(.width(16)) register_9 (
    .D(multiplexer_1_out), .en(decoder_1_out9), .Q(register_9_q), .clk(Clock), .clr(Reset));
  Register #(.width(16)) register_10 (
    .D(multiplexer_1_out), .en(decoder_1_out10), .Q(register_10_q), .clk(Clock), .clr(Reset));
  Register #(.width(16)) register_11 (
    .D(multiplexer_1_out), .en(decoder_1_out11), .Q(register_11_q), .clk(Clock), .clr(Reset));
  Register #(.width(16)) register_12 (
    .D(multiplexer_1_out), .en(decoder_1_out12), .Q(register_12_q), .clk(Clock), .clr(Reset));
  Register #(.width(16)) register_13 (
    .D(multiplexer_1_out), .en(decoder_1_out13), .Q(ram_data_address_extension), .clk(Clock), .clr(Reset));
  Register #(.width(16)) register_14 (
    .D(multiplexer_3_out), .en(or_4_out), .Q(instruction_address_extension), .clk(or_5_out), .clr(Reset));
  Register #(.width(16)) register_15 (
    .D(multiplexer_1_out), .en(decoder_1_out15), .Q(user_output), .clk(Clock), .clr(Reset));
  Multiplexer #(.select(4), .width(16)) multiplexer_4 (
    .in0({16{1'b0}}), .in1(register_1_q), .in2(register_2_q), .in3(register_3_q), .in4(register_4_q),
    .in5(register_5_q), .in6(register_6_q), .in7(register_7_q), .in8(register_8_q), .in9(register_9_q),
    .in10(register_10_q), .in11(register_11_q), .in12(register_12_q), .in13(ram_data_address_extension),
    .in14(instruction_address_extension), .in15(user_input), .out(output_1_Data_ALU),
    .sel(multiplexer_6_out), .en(or_7_out));
  Multiplexer #(.select(4), .width(16)) multiplexer_5 (
    .in0({16{1'b0}}), .in1(register_1_q), .in2(register_2_q), .in3(register_3_q), .in4(register_4_q),
    .in5(register_5_q), .in6(register_6_q), .in7(register_7_q), .in8(register_8_q), .in9(register_9_q),
    .in10(register_10_q), .in11(register_11_q), .in12(register_12_q), .in13(ram_data_address_extension),
    .in14(instruction_address_extension), .in15(user_input), .out(ALU_Output_2_Data),
    .sel(ALU_Output_2_Address), .en(or_6_out));
  buf or_6 (or_6_out, or_1_out);  // OR_Gate
  or or_7 (or_7_out, or_1_out, instruction_word_decoder_1_send_into_ram, or_2_out);
  Multiplexer #(.width(4)) multiplexer_6 (
    .in0(multiplexer_7_out), .in1(Jump_reg_check_Output_Address), .out(multiplexer_6_out), .sel(or_2_out),
    .en(or_7_out));
  Multiplexer #(.width(4), .enable("false")) multiplexer_7 (
    .in0(ALU_Output_1_Address), .in1(RAM_Output_Address), .out(multiplexer_7_out),
    .sel(instruction_word_decoder_1_send_into_ram));

  assign output_Data_Jump = output_1_Data_ALU;
  assign output_Data_Ram = output_1_Data_ALU;

  // Notes on the sheet:
  //   ALU
  //   ram counter overflow
  //   data line
  //   input output
  //   ram selector
  //   output 1 enable
  //   output 2 enable
endmodule

module instruction_decoder (
  input  [15:0] _16_bit_instruction,
  output [3:0] ALU_reg_address_2,
  output [3:0] ALU_reg_address_1,
  output [3:0] ALU_destination_register,
  output [3:0] word,
  output [3:0] constant,
  output [3:0] load_store_address,
  output [7:0] ram_address,
  output [3:0] jump_reg_check,
  output [7:0] jump_add_const
);


  assign ALU_destination_register = _16_bit_instruction[11:8];
  assign ALU_reg_address_1 = _16_bit_instruction[7:4];
  assign ALU_reg_address_2 = _16_bit_instruction[3:0];
  assign constant = _16_bit_instruction[3:0];
  assign jump_add_const = _16_bit_instruction[7:0];
  assign jump_reg_check = _16_bit_instruction[11:8];
  assign load_store_address = _16_bit_instruction[11:8];
  assign ram_address = _16_bit_instruction[7:0];
  assign word = _16_bit_instruction[15:12];

  // Notes on the sheet:
  //   config 2
  //   config 3/4
  //   config 1
  //   config 5/6
endmodule

module jump_controller (
  input  [3:0] word,
  input  [15:0] jump_comparison_data,
  input  [7:0] Current_Address,
  input  [7:0] address_constant,
  output jump,
  output [7:0] jump_address,
  output overflow_const_only
);

  wire comparator_1_eq, instruction_word_decoder_1_jump_number, instruction_word_decoder_1_jump_to_address,
       or_1_out;
  wire [7:0] adder_1_out;

  instruction_word_decoder instruction_word_decoder_1 (
    .Instruction(word), .jump_to_address(instruction_word_decoder_1_jump_to_address),
    .jump_number(instruction_word_decoder_1_jump_number));  // open: Math, Comp, load_into_reg, Shift, send_into_ram, halt, addi
  Comparator #(.width(16), .mode("unsigned")) comparator_1 (
    .a(jump_comparison_data), .b({16{1'b0}}), .eq(comparator_1_eq));  // open: gt, lt
  Adder adder_1 (
    .a(Current_Address), .b(address_constant), .out(adder_1_out), .cout(overflow_const_only));  // open: cin
  or or_1 (or_1_out, instruction_word_decoder_1_jump_to_address, instruction_word_decoder_1_jump_number);
  and and_1 (jump, or_1_out, comparator_1_eq);
  Multiplexer #(.width(8)) multiplexer_1 (
    .in0(address_constant), .in1(adder_1_out), .out(jump_address),
    .sel(instruction_word_decoder_1_jump_number), .en(jump));
endmodule

module CPU (
  input  Reset,
  input  Clock,
  input  [15:0] \input ,
  input  [15:0] RAM_DATA_In,
  output [15:0] \output ,
  output halt,
  output [23:0] Ram_Address,
  output [15:0] RAM_DATA_Out,
  output RAM_Clock,
  output Ram_store
);

  wire and_2_out, and_4_out, and_5_out, counter_2_carry, decoder_1_out0, decoder_1_out1, decoder_1_out2,
       instruction_word_decoder_1_load_into_reg, jump_controller_1_jump,
       jump_controller_1_overflow_const_only, not_1_out, or_1_out, or_2_out;
  wire [1:0] counter_1_q;
  wire [3:0] instruction_decoder_1_alu_destination_register, instruction_decoder_1_alu_reg_address_1,
       instruction_decoder_1_alu_reg_address_2, instruction_decoder_1_constant,
       instruction_decoder_1_jump_reg_check, instruction_decoder_1_load_store_address,
       instruction_decoder_1_word;
  wire [7:0] instruction_decoder_1_jump_add_const, jump_controller_1_jump_address;
  wire [15:0] alu_1_destination_output, demultiplexer_1_out0, demultiplexer_1_out1, register_1_q,
       registers_1_alu_output_2_data, registers_1_output_1_data_alu, registers_1_output_data_jump;
  wire [23:0] counter_2_q, registers_1_ram_data_address_extension;

  ALU alu_1 (
    .instruction(instruction_decoder_1_word), .input1(registers_1_output_1_data_alu),
    .input2(registers_1_alu_output_2_data), .input_2_const(instruction_decoder_1_constant),
    .destination_output(alu_1_destination_output));
  instruction_decoder instruction_decoder_1 (
    ._16_bit_instruction(register_1_q), .ALU_reg_address_2(instruction_decoder_1_alu_reg_address_2),
    .ALU_reg_address_1(instruction_decoder_1_alu_reg_address_1),
    .ALU_destination_register(instruction_decoder_1_alu_destination_register),
    .word(instruction_decoder_1_word), .constant(instruction_decoder_1_constant),
    .load_store_address(instruction_decoder_1_load_store_address),
    .ram_address(registers_1_ram_data_address_extension[7:0]),
    .jump_reg_check(instruction_decoder_1_jump_reg_check),
    .jump_add_const(instruction_decoder_1_jump_add_const));
  Registers registers_1 (
    .Clock(decoder_1_out2), .Reset(Reset), .Instruction(instruction_decoder_1_word),
    .ALU_Input_data(alu_1_destination_output),
    .ALU_Output_1_Address(instruction_decoder_1_alu_reg_address_1),
    .RAM_Output_Address(instruction_decoder_1_load_store_address), .RAM_Input_data(demultiplexer_1_out1),
    .ALU_Output_2_Address(instruction_decoder_1_alu_reg_address_2),
    .ALU_Input_data_address(instruction_decoder_1_alu_destination_register),
    .RAM_input_data_address(instruction_decoder_1_load_store_address), .user_input(\input ),
    .output_1_Data_ALU(registers_1_output_1_data_alu), .ALU_Output_2_Data(registers_1_alu_output_2_data),
    .user_output(\output ), .ram_counter_overflow(or_1_out),
    .instruction_address_extension(counter_2_q[23:8]), .output_Data_Ram(RAM_DATA_Out),
    .Jump_reg_check_Output_Address(instruction_decoder_1_jump_reg_check),
    .output_Data_Jump(registers_1_output_data_jump), .counter_clock(and_2_out),
    .ram_data_address_extension(registers_1_ram_data_address_extension[23:8]));
  Counter #(.width(2), .max('h3)) counter_1 (.Q(counter_1_q), .clk(Clock), .clr(Reset));  // open: load, D, count, carry
  instruction_word_decoder instruction_word_decoder_1 (
    .Instruction(instruction_decoder_1_word), .load_into_reg(instruction_word_decoder_1_load_into_reg),
    .send_into_ram(Ram_store), .halt(halt));  // open: Math, Comp, Shift, jump_to_address, jump_number, addi
  Decoder #(.select(2)) decoder_1 (
    .out0(decoder_1_out0), .out1(decoder_1_out1), .out2(decoder_1_out2), .out3(RAM_Clock), .sel(counter_1_q));  // open: en
  // AND_Gate and_1 has open pins: in0=Clock, in1=decoder_1_out0, out=open
  and and_2 (and_2_out, Clock, decoder_1_out1);
  // AND_Gate and_3 has open pins: in0=Clock, in1=decoder_1_out2, out=open
  and and_4 (and_4_out, Clock, RAM_Clock);
  Demultiplexer #(.width(16), .enable("false")) demultiplexer_1 (
    .out0(demultiplexer_1_out0), .out1(demultiplexer_1_out1), .in(RAM_DATA_In), .sel(and_5_out));
  and and_5 (and_5_out, or_2_out, instruction_word_decoder_1_load_into_reg);
  not not_1 (not_1_out, jump_controller_1_jump);
  jump_controller jump_controller_1 (
    .word(instruction_decoder_1_word), .jump_comparison_data(registers_1_output_data_jump),
    .Current_Address(counter_2_q[7:0]), .address_constant(instruction_decoder_1_jump_add_const),
    .jump(jump_controller_1_jump), .jump_address(jump_controller_1_jump_address),
    .overflow_const_only(jump_controller_1_overflow_const_only));
  Register #(.width(16)) register_1 (
    .D(demultiplexer_1_out0), .Q(register_1_q), .clk(decoder_1_out1), .clr(Reset));  // open: en
  Counter counter_2 (
    .load(jump_controller_1_jump), .D(jump_controller_1_jump_address), .count(not_1_out),
    .Q(counter_2_q[7:0]), .carry(counter_2_carry), .clk(decoder_1_out0), .clr(Reset));
  or or_1 (or_1_out, counter_2_carry, jump_controller_1_overflow_const_only);
  or or_2 (or_2_out, and_4_out, decoder_1_out2);
  Multiplexer #(.width(24), .enable("false")) multiplexer_1 (
    .in0(counter_2_q), .in1(registers_1_ram_data_address_extension), .out(Ram_Address), .sel(or_2_out));

  // Notes on the sheet:
  //   output
  //   input
  //   reset
  //   fetch
  //   execute
  //   select
  //   fetch
  //   execute
  //   save/finish
  //   jump
  //   instruction
  //   RAM
  //   counter
  //   store
  //   reset
  //   Instruction
  //   ram
endmodule
